# Fritzing sketch e-two (saved by Fritzing 0.9.4)
breadboards: 1

parts:
  Part1 = Arduino Uno (Rev3)
  Part2 = SparkFun ESP8266 Thing  # not connected
  U1 = LIPO-2000mAh [package=lipo-2000]
  Part3 = Bluetooth HC-05 Macho
  M2 = DC Motor
  M1 = DC Motor

nets:
  N1: Part1.D0/RX, Part3.TXD
  N2: Part1.D1/TX, Part3.RXD
  5V: Part1.5V, Part3.VCC
  N3: U1.+, M2.pin_2
  N4: Part3.GND, M2.pin_1, M1.pin_1
